// Logisim project PongV2.circ as structural Verilog: 3 circuits, main circuit main
module main (
  output [31:0] out_1
);

  wire cdm_8_1_p2, cdm_8_1_p4, cdm_8_1_p5, cdm_8_1_p6, cdm_8_1_p9, cdm_8_1_p10, cdm_8_1_p11,
       CHANGE_DIFFICULTY_out, Clk, clock_1_out, clock_2_out, Code, comparator_4_eq, comparator_4_gt,
       comparator_4_lt, comparator_5_eq, comparator_5_gt, comparator_5_lt, comparator_6_eq, comparator_6_gt,
       comparator_6_lt, data, decoder_3_out0, decoder_4_out1, decoder_5_out0, decoder_8_out1, decoder_9_out0,
       decoder_10_out0, decoder_11_out0, decoder_14_out0, I_O_Sel, IO_F8_out, IO_F9_out, IO_FA_out,
       IO_FB_out, IO_FC_out, IO_FD_out, IO_FE_out, IO_FF_out, mem, multiplexer_6_out, nand_1_out, not_1_out,
       not_2_out, not_3_out, not_4_out, or_5_out, or_6_out, or_7_out, or_9_out, or_10_out, P_Reset,
       pull_resistor_1_node, RAM, Rd_Wr, Reset, RESET_DIFFICULTY_out, RESET_out, undriven_3;
  wire [3:0] comparator_1_lt, I_O_Adr, joystick_1_y, LScore, RScore;
  wire [4:0] bit_extender_1_out, bitfinder_1_index, bitfinder_2_index;
  wire [7:0] bit_extender_2_out, bit_extender_3_out, cdm_8_1_p8, cdm_8_1_p15, cdm_8_1_p16, I_O_Dat,
       L_Paddle_Out, Paddle_Out, R_Paddle_Out, register_2_q, register_3_q, register_6_q, register_7_q,
       shifter_5_out, shifter_8_out, shifter_9_out, undriven, undriven_2;
  wire [7:4] cdm_8_1_p14, register_4_q, register_5_q;
  wire [15:0] decoder_6_out0, decoder_7_out0;
  wire [31:0] ai_1_test, BallX, BallY, controlled_buffer_1_out, LPad, multiplexer_1_out, multiplexer_2_out,
       multiplexer_3_out, multiplexer_4_out, multiplexer_5_out, multiplexer_7_out, multiplexer_8_out,
       multiplexer_9_out, multiplexer_10_out, multiplexer_11_out, multiplexer_12_out, multiplexer_13_out,
       multiplexer_14_out, multiplexer_15_out, multiplexer_16_out, multiplexer_17_out, multiplexer_18_out,
       multiplexer_19_out, multiplexer_20_out, multiplexer_21_out, multiplexer_22_out, multiplexer_23_out,
       multiplexer_24_out, multiplexer_25_out, multiplexer_26_out, multiplexer_27_out, multiplexer_28_out,
       multiplexer_29_out, multiplexer_30_out, multiplexer_31_out, multiplexer_32_out, multiplexer_33_out,
       multiplexer_34_out, or_1_out, or_2_out, or_3_out, or_4_out, shifter_1_out, shifter_2_out,
       shifter_6_out, shifter_7_out, xnor_1_out, xnor_2_out;

  // Probe on joystick_1_y
  Shifter #(.width(32)) shifter_1 (.in(out_1), .\dist (5'b00001), .out(shifter_1_out));
  Shifter #(.width(32), .shift("lr")) shifter_2 (.in(out_1), .\dist (5'b00001), .out(shifter_2_out));
  Comparator #(.width(5)) comparator_1 (.a(bit_extender_1_out), .b(5'b00110), .lt(comparator_1_lt[0]));  // open: gt, eq
  Comparator #(.width(5)) comparator_2 (.a(bit_extender_1_out), .b(5'b01010), .gt(comparator_1_lt[1]));  // open: eq, lt
  assign bit_extender_1_out = {{1{1'b0}}, joystick_1_y};  // Bit_Extender bit_extender_1
  Multiplexer #(.width(32), .enable("false")) multiplexer_1 (
    .in0({32{1'b0}}), .in1(BallY), .out(multiplexer_1_out), .sel(BallX[31]));
  Multiplexer #(.width(32), .enable("false")) multiplexer_2 (
    .in0({32{1'b0}}), .in1(BallY), .out(multiplexer_2_out), .sel(BallX[30]));
  assign controlled_buffer_1_out = not_1_out ? multiplexer_3_out : 32'bz;  // Controlled_Buffer controlled_buffer_1
  Multiplexer #(.select(4), .width(32), .enable("false")) multiplexer_3 (
    .in0(out_1), .in1(shifter_1_out), .in2(shifter_2_out), .in5(shifter_1_out), .in6(out_1), .in9(out_1),
    .in10(shifter_2_out), .out(multiplexer_3_out), .sel(comparator_1_lt));  // open: in3, in4, in7, in8, in11, in12, in13, in14, in15
  not not_1 (not_1_out, P_Reset);
  assign controlled_buffer_1_out = P_Reset ? 32'h1c000 : 32'bz;  // Controlled_Buffer controlled_buffer_2
  Clock #(.lowDuration(16)) clock_1 (.out(clock_1_out));
  Button button_1 ();  // open: out
  Joystick joystick_1 (.y(joystick_1_y));  // open: x
  Multiplexer #(.width(32), .enable("false")) multiplexer_4 (
    .in0({32{1'b0}}), .in1(BallY), .out(multiplexer_4_out), .sel(BallX[29]));
  Multiplexer #(.width(32), .enable("false")) multiplexer_5 (
    .in0({32{1'b0}}), .in1(BallY), .out(multiplexer_5_out), .sel(BallX[28]));
  Register #(.width(32), .trigger("falling")) register_1 (
    .D(controlled_buffer_1_out), .Q(out_1), .clk(multiplexer_6_out));  // open: en, clr
  Multiplexer #(.disabled(0), .enable("false")) multiplexer_6 (
    .in0(clock_1_out), .in1(Clk), .out(multiplexer_6_out), .sel(P_Reset));
  Multiplexer #(.width(32), .enable("false")) multiplexer_7 (
    .in0({32{1'b0}}), .in1(BallY), .out(multiplexer_7_out), .sel(BallX[27]));
  assign xnor_1_out = ~(32'hf0000000 ^ out_1);  // XNOR_Gate xnor_1, 32 bits wide
  assign xnor_2_out = ~(32'hf ^ out_1);  // XNOR_Gate xnor_2, 32 bits wide
  Multiplexer #(.width(32), .enable("false")) multiplexer_8 (
    .in0({32{1'b0}}), .in1(BallY), .out(multiplexer_8_out), .sel(BallX[26]));
  Multiplexer #(.width(32), .enable("false")) multiplexer_9 (
    .in0({32{1'b0}}), .in1(BallY), .out(multiplexer_9_out), .sel(BallX[25]));
  // Probe on bitfinder_1_index
  BitFinder #(.width(32)) bitfinder_1 (.in(out_1), .index(bitfinder_1_index));  // open: found
  and and_1 (comparator_1_lt[3], xnor_1_out[29], xnor_1_out[30], xnor_1_out[31]);
  and and_2 (comparator_1_lt[2], xnor_2_out[0], xnor_2_out[1], xnor_2_out[2]);
  Multiplexer #(.width(32), .enable("false")) multiplexer_10 (
    .in0({32{1'b0}}), .in1(BallY), .out(multiplexer_10_out), .sel(BallX[24]));
  assign bit_extender_2_out = {{3{1'b0}}, bitfinder_1_index};  // Bit_Extender bit_extender_2
  Multiplexer #(.width(32), .enable("false")) multiplexer_11 (
    .in0({32{1'b0}}), .in1(BallY), .out(multiplexer_11_out), .sel(BallX[22]));
  Multiplexer #(.width(32), .enable("false")) multiplexer_12 (
    .in0({32{1'b0}}), .in1(BallY), .out(multiplexer_12_out), .sel(BallX[23]));
  // Probe on Paddle_Out
  Shifter shifter_3 (.in(bit_extender_2_out), .\dist (3'b011), .out(Paddle_Out));
  Hex_Digit_Display hex_digit_display_1 (.value(LScore));  // open: dp
  Multiplexer #(.width(32), .enable("false")) multiplexer_13 (
    .in0({32{1'b0}}), .in1(BallY), .out(multiplexer_13_out), .sel(BallX[21]));
  Multiplexer #(.width(32), .enable("false")) multiplexer_14 (
    .in0({32{1'b0}}), .in1(BallY), .out(multiplexer_14_out), .sel(BallX[20]));
  DotMatrix #(.matrixcols(32), .matrixrows(32)) dotmatrix_1 (
    .col0(or_1_out), .col1(multiplexer_2_out), .col2(multiplexer_4_out), .col3(multiplexer_5_out),
    .col4(multiplexer_7_out), .col5(multiplexer_8_out), .col6(multiplexer_9_out), .col7(multiplexer_10_out),
    .col8(multiplexer_12_out), .col9(multiplexer_11_out), .col10(multiplexer_13_out),
    .col11(multiplexer_14_out), .col12(multiplexer_15_out), .col13(multiplexer_17_out),
    .col14(multiplexer_16_out), .col15(or_2_out), .col16(or_3_out), .col17(multiplexer_19_out),
    .col18(multiplexer_22_out), .col19(multiplexer_21_out), .col20(multiplexer_23_out),
    .col21(multiplexer_25_out), .col22(multiplexer_24_out), .col23(multiplexer_26_out),
    .col24(multiplexer_27_out), .col25(multiplexer_28_out), .col26(multiplexer_30_out),
    .col27(multiplexer_29_out), .col28(multiplexer_31_out), .col29(multiplexer_32_out),
    .col30(multiplexer_33_out), .col31(or_4_out));
  assign or_1_out = LPad | multiplexer_1_out;  // OR_Gate or_1, 32 bits wide
  Multiplexer #(.width(32), .enable("false")) multiplexer_15 (
    .in0({32{1'b0}}), .in1(BallY), .out(multiplexer_15_out), .sel(BallX[19]));
  Multiplexer #(.width(32), .enable("false")) multiplexer_16 (
    .in0({32{1'b0}}), .in1(BallY), .out(multiplexer_16_out), .sel(BallX[17]));
  Multiplexer #(.width(32), .enable("false")) multiplexer_17 (
    .in0({32{1'b0}}), .in1(BallY), .out(multiplexer_17_out), .sel(BallX[18]));
  assign or_2_out = 32'haaaaaaaa | multiplexer_18_out;  // OR_Gate or_2, 32 bits wide
  Multiplexer #(.width(32), .enable("false")) multiplexer_18 (
    .in0({32{1'b0}}), .in1(BallY), .out(multiplexer_18_out), .sel(BallX[16]));
  assign or_3_out = multiplexer_20_out | 32'h55555555;  // OR_Gate or_3, 32 bits wide
  Multiplexer #(.width(32), .enable("false")) multiplexer_19 (
    .in0({32{1'b0}}), .in1(BallY), .out(multiplexer_19_out), .sel(BallX[14]));
  Multiplexer #(.width(32), .enable("false")) multiplexer_20 (
    .in0({32{1'b0}}), .in1(BallY), .out(multiplexer_20_out), .sel(BallX[15]));
  Hex_Digit_Display hex_digit_display_2 (.value(RScore));  // open: dp
  assign or_4_out = out_1 | multiplexer_34_out;  // OR_Gate or_4, 32 bits wide
  Multiplexer #(.width(32), .enable("false")) multiplexer_21 (
    .in0({32{1'b0}}), .in1(BallY), .out(multiplexer_21_out), .sel(BallX[12]));
  Multiplexer #(.width(32), .enable("false")) multiplexer_22 (
    .in0({32{1'b0}}), .in1(BallY), .out(multiplexer_22_out), .sel(BallX[13]));
  // Probe on cdm_8_1_p2
  // Probe on cdm_8_1_p4
  Button button_2 (.out(Reset));
  and and_3 (Clk, ~pull_resistor_1_node, clock_2_out);  // AND_Gate
  Pull_Resistor pull_resistor_1 (.node(pull_resistor_1_node));
  Clock clock_2 (.out(clock_2_out));
  Comparator comparator_3 (.a(cdm_8_1_p8), .b(undriven), .eq(pull_resistor_1_node));  // open: gt, lt
  Multiplexer #(.width(32), .enable("false")) multiplexer_23 (
    .in0({32{1'b0}}), .in1(BallY), .out(multiplexer_23_out), .sel(BallX[11]));
  // Probe on cdm_8_1_p8
  // Probe on cdm_8_1_p6
  // Probe on cdm_8_1_p5
  and and_4 (I_O_Sel, not_3_out, Clk, data);
  Multiplexer #(.width(32), .enable("false")) multiplexer_24 (
    .in0({32{1'b0}}), .in1(BallY), .out(multiplexer_24_out), .sel(BallX[9]));
  Multiplexer #(.width(32), .enable("false")) multiplexer_25 (
    .in0({32{1'b0}}), .in1(BallY), .out(multiplexer_25_out), .sel(BallX[10]));
  // Probe on cdm_8_1_p10
  // Probe on cdm_8_1_p9
  Multiplexer #(.width(32), .enable("false")) multiplexer_26 (
    .in0({32{1'b0}}), .in1(BallY), .out(multiplexer_26_out), .sel(BallX[8]));
  Decoder #(.disabled(0)) decoder_1 (.out0(Code), .out1(data), .sel(cdm_8_1_p11), .en(mem));
  not not_2 (not_2_out, Rd_Wr);
  assign I_O_Dat = not_2_out ? cdm_8_1_p15 : 8'bz;  // Controlled_Buffer controlled_buffer_3
  // CdM_8 cdm_8_1: pin names not known; wires that end beside it: Clk, cdm_8_1_p2, Reset, cdm_8_1_p4, cdm_8_1_p5, cdm_8_1_p6, 8'h45, cdm_8_1_p8, cdm_8_1_p9, cdm_8_1_p10, cdm_8_1_p11, mem, Rd_Wr, {cdm_8_1_p14, I_O_Adr}, cdm_8_1_p15, cdm_8_1_p16
  assign cdm_8_1_p16 = Rd_Wr ? I_O_Dat : 8'bz;  // Controlled_Buffer controlled_buffer_4
  not not_3 (not_3_out, nand_1_out);
  nand nand_1 (nand_1_out, cdm_8_1_p14[7], cdm_8_1_p14[6], cdm_8_1_p14[5], cdm_8_1_p14[4]);
  and and_5 (RAM, nand_1_out, data);
  Multiplexer #(.width(32), .enable("false")) multiplexer_27 (
    .in0({32{1'b0}}), .in1(BallY), .out(multiplexer_27_out), .sel(BallX[7]));
  Multiplexer #(.width(32), .enable("false")) multiplexer_28 (
    .in0({32{1'b0}}), .in1(BallY), .out(multiplexer_28_out), .sel(BallX[6]));
  Multiplexer #(.width(32), .enable("false")) multiplexer_29 (
    .in0({32{1'b0}}), .in1(BallY), .out(multiplexer_29_out), .sel(BallX[4]));
  Multiplexer #(.width(32), .enable("false")) multiplexer_30 (
    .in0({32{1'b0}}), .in1(BallY), .out(multiplexer_30_out), .sel(BallX[5]));
  // Probe on {cdm_8_1_p14, I_O_Adr}
  Multiplexer #(.width(32), .enable("false")) multiplexer_31 (
    .in0({32{1'b0}}), .in1(BallY), .out(multiplexer_31_out), .sel(BallX[3]));
  ROM rom_1 (.addr({cdm_8_1_p14, I_O_Adr}), .data(I_O_Dat), .sel(Code));
  RAM ram_1 (.addr({cdm_8_1_p14, I_O_Adr}), .data(I_O_Dat), .sel(RAM), .clk(Clk), .ld(Rd_Wr));  // open: clr
  Multiplexer #(.width(32), .enable("false")) multiplexer_32 (
    .in0({32{1'b0}}), .in1(BallY), .out(multiplexer_32_out), .sel(BallX[2]));
  Multiplexer #(.width(32), .enable("false")) multiplexer_33 (
    .in0({32{1'b0}}), .in1(BallY), .out(multiplexer_33_out), .sel(BallX[1]));
  Multiplexer #(.width(32), .enable("false")) multiplexer_34 (
    .in0({32{1'b0}}), .in1(BallY), .out(multiplexer_34_out), .sel(BallX[0]));
  // Probe on I_O_Dat
  and IO_F8 (IO_F8_out, I_O_Sel, ~I_O_Adr[0], ~I_O_Adr[1], ~I_O_Adr[2], I_O_Adr[3]);  // AND_Gate
  Decoder #(.disabled(0)) decoder_2 (.out0(P_Reset), .sel(Rd_Wr), .en(IO_F8_out));  // open: out1
  Register register_2 (.D(I_O_Dat), .Q(register_2_q), .clk(decoder_3_out0));  // open: en, clr
  // Probe on BallY
  Button RESET_DIFFICULTY (.out(RESET_DIFFICULTY_out));
  and IO_F9 (IO_F9_out, I_O_Sel, I_O_Adr[0], ~I_O_Adr[1], ~I_O_Adr[2], I_O_Adr[3]);  // AND_Gate
  Decoder #(.disabled(0)) decoder_3 (.out0(decoder_3_out0), .sel(Rd_Wr), .en(IO_F9_out));  // open: out1
  Button CHANGE_DIFFICULTY (.out(CHANGE_DIFFICULTY_out));
  or or_5 (or_5_out, RESET_out, P_Reset);
  Button u_RESET (.out(RESET_out));
  // Probe on ai_1_test
  not not_4 (not_4_out, register_2_q[0]);
  AI ai_1 (
    .Ball_Input(BallY), .Change_Difficulty(RESET_DIFFICULTY_out), .Reset_Difficulty(CHANGE_DIFFICULTY_out),
    .TEST(ai_1_test), .Reset(or_5_out), .Output(LPad), .enable(or_6_out));
  or or_6 (or_6_out, not_4_out, or_5_out);
  // Probe on LPad
  // Probe on bitfinder_2_index
  BitFinder #(.width(32)) bitfinder_2 (.in(LPad), .index(bitfinder_2_index));  // open: found
  assign bit_extender_3_out = {{3{1'b0}}, bitfinder_2_index};  // Bit_Extender bit_extender_3
  // Probe on L_Paddle_Out
  Shifter shifter_4 (.in(bit_extender_3_out), .\dist (3'b011), .out(L_Paddle_Out));
  assign I_O_Dat = decoder_4_out1 ? L_Paddle_Out : 8'bz;  // Controlled_Buffer controlled_buffer_5
  and IO_FA (IO_FA_out, I_O_Sel, ~I_O_Adr[0], I_O_Adr[1], ~I_O_Adr[2], I_O_Adr[3]);  // AND_Gate
  Decoder #(.disabled(0)) decoder_4 (.out1(decoder_4_out1), .sel(Rd_Wr), .en(IO_FA_out));  // open: out0
  Register register_3 (.D(undriven_2), .Q(register_3_q), .clk(decoder_5_out0));  // open: en, clr
  // Probe on register_3_q
  Shifter #(.shift("lr")) shifter_5 (.in(register_3_q), .\dist (3'b011), .out(shifter_5_out));
  Decoder #(.disabled(0)) decoder_5 (.out0(decoder_5_out0), .en(undriven_3));  // open: out1, sel
  // Probe on shifter_5_out
  // Probe on shifter_5_out[3:0]
  Comparator #(.mode("unsigned")) comparator_4 (
    .a(register_3_q), .b(8'h7f), .gt(comparator_4_gt), .eq(comparator_4_eq), .lt(comparator_4_lt));
  // Probe on shifter_5_out[3:0]
  Decoder #(.select(4), .disabled(0)) decoder_6 (
    .out0(decoder_6_out0[0]), .out1(decoder_6_out0[1]), .out2(decoder_6_out0[2]), .out3(decoder_6_out0[3]),
    .out4(decoder_6_out0[4]), .out5(decoder_6_out0[5]), .out6(decoder_6_out0[6]), .out7(decoder_6_out0[7]),
    .out8(decoder_6_out0[8]), .out9(decoder_6_out0[9]), .out10(decoder_6_out0[10]),
    .out11(decoder_6_out0[11]), .out12(decoder_6_out0[12]), .out13(decoder_6_out0[13]),
    .out14(decoder_6_out0[14]), .out15(decoder_6_out0[15]), .sel(shifter_5_out[3:0]), .en(comparator_4_lt));
  Decoder #(.select(4), .disabled(0)) decoder_7 (
    .out0(decoder_7_out0[0]), .out1(decoder_7_out0[1]), .out2(decoder_7_out0[2]), .out3(decoder_7_out0[3]),
    .out4(decoder_7_out0[4]), .out5(decoder_7_out0[5]), .out6(decoder_7_out0[6]), .out7(decoder_7_out0[7]),
    .out8(decoder_7_out0[8]), .out9(decoder_7_out0[9]), .out10(decoder_7_out0[10]),
    .out11(decoder_7_out0[11]), .out12(decoder_7_out0[12]), .out13(decoder_7_out0[13]),
    .out14(decoder_7_out0[14]), .out15(decoder_7_out0[15]), .sel(shifter_5_out[3:0]), .en(or_7_out));
  or or_7 (or_7_out, comparator_4_gt, comparator_4_eq);
  // Probe on {decoder_7_out0, decoder_6_out0}
  // OR_Gate or_8 has open pins: in0={decoder_7_out0, decoder_6_out0}, in1=shifter_7_out, in2=shifter_6_out, out=open
  Shifter #(.width(32)) shifter_6 (.in({decoder_7_out0, decoder_6_out0}), .\dist (5'b00001), .out(shifter_6_out));
  Shifter #(.width(32), .shift("lr")) shifter_7 (
    .in({decoder_7_out0, decoder_6_out0}), .\dist (5'b00001), .out(shifter_7_out));
  assign I_O_Dat = decoder_8_out1 ? R_Paddle_Out : 8'bz;  // Controlled_Buffer controlled_buffer_6
  and IO_FB (IO_FB_out, I_O_Sel, I_O_Adr[0], I_O_Adr[1], ~I_O_Adr[2], I_O_Adr[3]);  // AND_Gate
  Decoder #(.disabled(0)) decoder_8 (.out1(decoder_8_out1), .sel(Rd_Wr), .en(IO_FB_out));  // open: out0
  Register register_4 (.D(I_O_Dat), .Q({register_4_q, LScore}), .clk(decoder_9_out0));  // open: en, clr
  and IO_FC (IO_FC_out, I_O_Sel, ~I_O_Adr[0], ~I_O_Adr[1], I_O_Adr[2], I_O_Adr[3]);  // AND_Gate
  Hex_Digit_Display hex_digit_display_3 (.value(LScore));  // open: dp
  Decoder #(.disabled(0)) decoder_9 (.out0(decoder_9_out0), .sel(Rd_Wr), .en(IO_FC_out));  // open: out1
  Register register_5 (.D(I_O_Dat), .Q({register_5_q, RScore}), .clk(decoder_10_out0));  // open: en, clr
  Hex_Digit_Display hex_digit_display_4 (.value(RScore));  // open: dp
  and IO_FD (IO_FD_out, I_O_Sel, I_O_Adr[0], ~I_O_Adr[1], I_O_Adr[2], I_O_Adr[3]);  // AND_Gate
  Decoder #(.disabled(0)) decoder_10 (.out0(decoder_10_out0), .sel(Rd_Wr), .en(IO_FD_out));  // open: out1
  Register register_6 (.D(I_O_Dat), .Q(register_6_q), .clk(decoder_11_out0));  // open: en, clr
  // Probe on register_6_q
  and IO_FE (IO_FE_out, I_O_Sel, ~I_O_Adr[0], I_O_Adr[1], I_O_Adr[2], I_O_Adr[3]);  // AND_Gate
  Decoder #(.disabled(0)) decoder_11 (.out0(decoder_11_out0), .sel(Rd_Wr), .en(IO_FE_out));  // open: out1
  // Probe on shifter_8_out
  Shifter #(.shift("lr")) shifter_8 (.in(register_6_q), .\dist (3'b011), .out(shifter_8_out));
  // Probe on shifter_8_out[3:0]
  Comparator #(.mode("unsigned")) comparator_5 (
    .a(register_6_q), .b(8'h7f), .gt(comparator_5_gt), .eq(comparator_5_eq), .lt(comparator_5_lt));
  // Probe on shifter_8_out[3:0]
  Decoder #(.select(4), .disabled(0)) decoder_12 (
    .out0(BallX[0]), .out1(BallX[1]), .out2(BallX[2]), .out3(BallX[3]), .out4(BallX[4]), .out5(BallX[5]),
    .out6(BallX[6]), .out7(BallX[7]), .out8(BallX[8]), .out9(BallX[9]), .out10(BallX[10]), .out11(BallX[11]),
    .out12(BallX[12]), .out13(BallX[13]), .out14(BallX[14]), .out15(BallX[15]), .sel(shifter_8_out[3:0]),
    .en(comparator_5_lt));
  Decoder #(.select(4), .disabled(0)) decoder_13 (
    .out0(BallX[16]), .out1(BallX[17]), .out2(BallX[18]), .out3(BallX[19]), .out4(BallX[20]),
    .out5(BallX[21]), .out6(BallX[22]), .out7(BallX[23]), .out8(BallX[24]), .out9(BallX[25]),
    .out10(BallX[26]), .out11(BallX[27]), .out12(BallX[28]), .out13(BallX[29]), .out14(BallX[30]),
    .out15(BallX[31]), .sel(shifter_8_out[3:0]), .en(or_9_out));
  or or_9 (or_9_out, comparator_5_gt, comparator_5_eq);
  // Probe on BallX
  and IO_FF (IO_FF_out, I_O_Sel, I_O_Adr[0], I_O_Adr[1], I_O_Adr[2], I_O_Adr[3]);
  Register register_7 (.D(I_O_Dat), .Q(register_7_q), .clk(decoder_14_out0));  // open: en, clr
  // Probe on register_7_q
  Shifter #(.shift("lr")) shifter_9 (.in(register_7_q), .\dist (3'b011), .out(shifter_9_out));
  Decoder #(.disabled(0)) decoder_14 (.out0(decoder_14_out0), .sel(Rd_Wr), .en(IO_FF_out));  // open: out1
  // Probe on shifter_9_out
  Comparator #(.mode("unsigned")) comparator_6 (
    .a(register_7_q), .b(8'h7f), .gt(comparator_6_gt), .eq(comparator_6_eq), .lt(comparator_6_lt));
  // Probe on shifter_9_out[3:0]
  or or_10 (or_10_out, comparator_6_gt, comparator_6_eq);
  // Probe on shifter_9_out[3:0]
  Decoder #(.select(4), .disabled(0)) decoder_15 (
    .out0(BallY[0]), .out1(BallY[1]), .out2(BallY[2]), .out3(BallY[3]), .out4(BallY[4]), .out5(BallY[5]),
    .out6(BallY[6]), .out7(BallY[7]), .out8(BallY[8]), .out9(BallY[9]), .out10(BallY[10]), .out11(BallY[11]),
    .out12(BallY[12]), .out13(BallY[13]), .out14(BallY[14]), .out15(BallY[15]), .sel(shifter_9_out[3:0]),
    .en(comparator_6_lt));
  Decoder #(.select(4), .disabled(0)) decoder_16 (
    .out0(BallY[16]), .out1(BallY[17]), .out2(BallY[18]), .out3(BallY[19]), .out4(BallY[20]),
    .out5(BallY[21]), .out6(BallY[22]), .out7(BallY[23]), .out8(BallY[24]), .out9(BallY[25]),
    .out10(BallY[26]), .out11(BallY[27]), .out12(BallY[28]), .out13(BallY[29]), .out14(BallY[30]),
    .out15(BallY[31]), .sel(shifter_9_out[3:0]), .en(or_10_out));
  // Probe on BallY

  // Other names for the same wires on the sheet: RPad[31:0] = out_1

  // Notes on the sheet:
  //   contents of rom_1 (hex, n*v repeats v):
  //   d0 8 d1 e1 a4 d0 4 d1 e2 a4 ee 12 ee 24 ee 49 ee e d0 dc b0 d1 0 a1 d0 fc a1 d0 dd b0 a1 d0 fd a1 ee
  //   24 d0 de d1 fd f5 a1 d2 fe d0 df d1 fe f5 a1 d0 ff a9 a1 ee 38 d0 da d2 db d1 ff f5 a1 a9 d0 f8 d2
  //   f8 a1 a9 ee e d0 de b0 d1 5 71 e3 58 d1 fa 71 e8 5e ee 6a d0 dd d2 fd ee 64 d0 dc d2 fc ee 64 b1 8d
  //   a1 a9 ee c d0 de b0 d1 10 71 e3 7d d1 ef 71 e8 79 ee b6 d0 fa ee 81 d0 fb ee 81 b0 d2 df ba d1 12 11
  //   78 e2 8d ee b6 79 e9 92 ee b6 d1 ef 79 e2 ac d1 3 11 79 e9 a5 d1 10 11 79 e2 a5 ee ac d3 e6 bd 81 ad
  //   ee ac d0 e0 b1 81 d2 f9 a9 a1 ee b6 d0 df b0 d1 8 d2 f7 71 e9 c5 72 e2 c5 ee cc d3 e6 be 82 ae ee cc
  //   d0 e1 b0 d1 e2 b5 ee d4 d2 de bb d2 e0 ba a e0 e0 1c ee e1 3c d2 de a8 d2 df bb d2 e6 ba a e0 f0 1d
  //   ee f1 3d d2 df a9 d3 fe d2 ff ac a9 ee e d4 80 80 80
  //   Paddle input -F8
  //   FA-Left Paddle
  //   FB-Right Paddle
  //   FC - Left Score
  //   FD - Right Score
  //   FE - Ball X
  //   FF - Ball Y
endmodule

module CDM8 (
);

  wire and_2_out, cdm_8_1_p2, cdm_8_1_p4, cdm_8_1_p5, cdm_8_1_p6, cdm_8_1_p7, cdm_8_1_p8, cdm_8_1_p9,
       cdm_8_1_p10, Clk, decoder_1_out0, decoder_1_out1, decoder_1_out2, decoder_1_out3, decoder_1_out4,
       decoder_1_out5, decoder_1_out6, decoder_1_out7, I_O_Sel, not_1_out, not_2_out, Rd_Wr, Reset;
  wire [2:0] I_O_Adr;
  wire [7:0] cdm_8_1_p13, cdm_8_1_p14, I_O_Dat;
  wire [7:3] cdm_8_1_p12;

  // Probe on cdm_8_1_p2
  Button button_1 (.out(Reset));
  Clock clock_1 (.out(Clk));
  Decoder #(.select(3)) decoder_1 (
    .out0(decoder_1_out0), .out1(decoder_1_out1), .out2(decoder_1_out2), .out3(decoder_1_out3),
    .out4(decoder_1_out4), .out5(decoder_1_out5), .out6(decoder_1_out6), .out7(decoder_1_out7),
    .sel(I_O_Adr), .en(I_O_Sel));
  // Probe on cdm_8_1_p6
  // Probe on cdm_8_1_p5
  // Probe on cdm_8_1_p4
  Keyboard keyboard_1 ();  // open: clk, re, clr, avail, data
  LED led_1 (.in(decoder_1_out0));
  LED led_2 (.in(decoder_1_out1));
  LED led_3 (.in(decoder_1_out2));
  LED led_4 (.in(decoder_1_out3));
  // Probe on cdm_8_1_p8
  // Probe on cdm_8_1_p7
  LED led_5 (.in(decoder_1_out4));
  LED led_6 (.in(decoder_1_out5));
  LED led_7 (.in(decoder_1_out6));
  LED led_8 (.in(decoder_1_out7));
  // Probe on cdm_8_1_p9
  not not_1 (not_1_out, Rd_Wr);
  // CdM_8 cdm_8_1: pin names not known; wires that end beside it: Clk, cdm_8_1_p2, Reset, cdm_8_1_p4, cdm_8_1_p5, cdm_8_1_p6, cdm_8_1_p7, cdm_8_1_p8, cdm_8_1_p9, cdm_8_1_p10, Rd_Wr, {cdm_8_1_p12, I_O_Adr}, cdm_8_1_p13, cdm_8_1_p14, Rd_Wr
  assign I_O_Dat = not_1_out ? cdm_8_1_p13 : 8'bz;  // Controlled_Buffer controlled_buffer_1
  assign cdm_8_1_p14 = Rd_Wr ? I_O_Dat : 8'bz;  // Controlled_Buffer controlled_buffer_2
  not not_2 (not_2_out, I_O_Sel);
  and and_1 (I_O_Sel, cdm_8_1_p10, cdm_8_1_p12[7], cdm_8_1_p12[6], cdm_8_1_p12[5], cdm_8_1_p12[4], cdm_8_1_p12[3]);
  // Probe on {cdm_8_1_p12, I_O_Adr}
  and and_2 (and_2_out, cdm_8_1_p10, not_2_out);
  // Probe on I_O_Dat
  RAM ram_1 (.addr({cdm_8_1_p12, I_O_Adr}), .data(I_O_Dat), .sel(and_2_out), .clk(Clk), .ld(Rd_Wr));  // open: clr
endmodule

module AI (
  input  enable,
  input  Reset,
  input  [31:0] Ball_Input,
  input  Change_Difficulty,
  input  Reset_Difficulty,
  output [31:0] Output,
  output [31:0] TEST
);

  wire clock_1_out, clock_2_out, clock_3_out, clock_4_out, comparator_1_eq, controlled_buffer_7_out,
       multiplexer_2_out, not_1_out, not_2_out, not_3_out;
  wire [2:0] controlled_buffer_5_out, register_2_q, shifter_5_out;
  wire [3:0] comparator_1_lt, controlled_buffer_1_out;
  wire [4:0] bitfinder_1_index;
  wire [31:0] controlled_buffer_3_out, multiplexer_1_out, shifter_1_out, shifter_2_out, shifter_3_out,
       xnor_1_out, xnor_2_out;

  BitFinder #(.width(32)) bitfinder_1 (.in(Output), .index(bitfinder_1_index));  // open: found
  Comparator #(.width(32)) comparator_1 (
    .a(TEST), .b(Ball_Input), .gt(comparator_1_lt[1]), .eq(comparator_1_eq), .lt(comparator_1_lt[0]));
  Shifter #(.width(32), .shift("rl")) shifter_1 (.in(32'h80000000), .\dist (bitfinder_1_index), .out(shifter_1_out));
  Shifter #(.width(32)) shifter_2 (.in(Output), .\dist (5'b00001), .out(shifter_2_out));
  Shifter #(.width(32), .shift("lr")) shifter_3 (.in(Output), .\dist (5'b00001), .out(shifter_3_out));
  Shifter #(.width(32), .shift("rl")) shifter_4 (.in(shifter_1_out), .\dist (5'b00010), .out(TEST));
  Multiplexer #(.select(4), .width(32), .enable("false")) multiplexer_1 (
    .in0(Output), .in1(shifter_2_out), .in2(shifter_3_out), .in5(shifter_2_out), .in6(Output), .in9(Output),
    .in10(shifter_3_out), .out(multiplexer_1_out), .sel(controlled_buffer_1_out));  // open: in3, in4, in7, in8, in11, in12, in13, in14, in15
  assign controlled_buffer_1_out = comparator_1_eq ? 4'b0000 : 4'bz;  // Controlled_Buffer controlled_buffer_1
  assign controlled_buffer_1_out = not_1_out ? comparator_1_lt : 4'bz;  // Controlled_Buffer controlled_buffer_2
  not not_1 (not_1_out, comparator_1_eq);
  assign controlled_buffer_3_out = not_2_out ? multiplexer_1_out : 32'bz;  // Controlled_Buffer controlled_buffer_3
  not not_2 (not_2_out, Reset);
  assign controlled_buffer_3_out = Reset ? 32'h1c000 : 32'bz;  // Controlled_Buffer controlled_buffer_4
  Clock clock_1 (.out(clock_1_out));
  not not_3 (not_3_out, Change_Difficulty);
  assign controlled_buffer_5_out = not_3_out ? shifter_5_out : 3'bz;  // Controlled_Buffer controlled_buffer_5
  assign controlled_buffer_5_out = Change_Difficulty ? 3'b001 : 3'bz;  // Controlled_Buffer controlled_buffer_6
  Register #(.width(32), .trigger("falling")) register_1 (
    .D(controlled_buffer_3_out), .Q(Output), .clk(controlled_buffer_7_out));  // open: en, clr
  assign controlled_buffer_7_out = enable ? multiplexer_2_out : 1'bz;  // Controlled_Buffer controlled_buffer_7
  Multiplexer #(.select(3)) multiplexer_2 (
    .in0(clock_1_out), .in1(clock_1_out), .in2(clock_3_out), .in4(clock_2_out), .out(multiplexer_2_out),
    .sel(shifter_5_out), .en(1'b1));  // open: in3, in5, in6, in7
  Clock #(.highDuration(10)) clock_2 (.out(clock_2_out));
  Clock #(.highDuration(5)) clock_3 (.out(clock_3_out));
  Clock clock_4 (.out(clock_4_out));
  // Probe on shifter_5_out
  Register #(.width(3)) register_2 (.D(controlled_buffer_5_out), .Q(register_2_q), .clk(clock_4_out));  // open: en, clr
  Shifter #(.width(3), .shift("rl")) shifter_5 (
    .in(register_2_q), .\dist ({1'b0, Reset_Difficulty}), .out(shifter_5_out));
  assign xnor_1_out = ~(32'he0000000 ^ Output);  // XNOR_Gate xnor_1, 32 bits wide
  and and_1 (comparator_1_lt[3], xnor_1_out[29], xnor_1_out[30], xnor_1_out[31]);
  assign xnor_2_out = ~(32'h7 ^ Output);  // XNOR_Gate xnor_2, 32 bits wide
  and and_2 (comparator_1_lt[2], xnor_2_out[0], xnor_2_out[1], xnor_2_out[2]);
endmodule
