// Logisim project TvTennis 0.02.circ as structural Verilog: 2 circuits, main circuit main
module main (
  input  [31:0] in_1,
  input  [29:0] Y_Axis,
  input  [31:0] X_Axis
);

  wire Clock, DOWN_2_out, DOWN_out, RESET_2_out, RESET_out, UP_2_out, UP_out;
  wire [1:0] button_1_out;
  wire [31:0] multiplexer_1_out, multiplexer_2_out, multiplexer_3_out, multiplexer_4_out, multiplexer_5_out,
       multiplexer_6_out, multiplexer_7_out, multiplexer_8_out, multiplexer_9_out, multiplexer_10_out,
       multiplexer_11_out, multiplexer_12_out, multiplexer_13_out, multiplexer_14_out, multiplexer_15_out,
       multiplexer_16_out, multiplexer_17_out, multiplexer_18_out, multiplexer_19_out, multiplexer_20_out,
       multiplexer_21_out, multiplexer_22_out, multiplexer_23_out, multiplexer_24_out, multiplexer_25_out,
       multiplexer_26_out, multiplexer_27_out, multiplexer_28_out, multiplexer_29_out, multiplexer_30_out,
       multiplexer_31_out, paddle_shift_1_out_4, paddle_shift_2_out_4, register_1_q, shifter_1_out,
       shifter_2_out;

  Multiplexer #(.width(32), .enable("false")) multiplexer_1 (
    .in0({32{1'b0}}), .in1(X_Axis), .out(multiplexer_1_out), .sel(Y_Axis[0]));
  Multiplexer #(.width(32), .enable("false")) multiplexer_2 (
    .in0({32{1'b0}}), .in1(X_Axis), .out(multiplexer_2_out), .sel(Y_Axis[1]));
  Multiplexer #(.width(32), .enable("false")) multiplexer_3 (
    .in0({32{1'b0}}), .in1(X_Axis), .out(multiplexer_3_out), .sel(Y_Axis[2]));
  Multiplexer #(.width(32), .enable("false")) multiplexer_4 (
    .in0({32{1'b0}}), .in1(X_Axis), .out(multiplexer_4_out), .sel(Y_Axis[3]));
  Multiplexer #(.width(32), .enable("false")) multiplexer_5 (
    .in0({32{1'b0}}), .in1(X_Axis), .out(multiplexer_5_out), .sel(Y_Axis[4]));
  Button RESET (.out(RESET_out));
  Multiplexer #(.width(32), .enable("false")) multiplexer_6 (
    .in0({32{1'b0}}), .in1(X_Axis), .out(multiplexer_6_out), .sel(Y_Axis[6]));
  Multiplexer #(.width(32), .enable("false")) multiplexer_7 (
    .in0({32{1'b0}}), .in1(X_Axis), .out(multiplexer_7_out), .sel(Y_Axis[5]));
  Button UP (.out(UP_out));
  Button DOWN (.out(DOWN_out));
  Multiplexer #(.width(32), .enable("false")) multiplexer_8 (
    .in0({32{1'b0}}), .in1(X_Axis), .out(multiplexer_8_out), .sel(Y_Axis[7]));
  Hex_Digit_Display hex_digit_display_1 ();  // open: value, dp
  DotMatrix #(.matrixcols(32), .matrixrows(32)) dotmatrix_1 (
    .col0(paddle_shift_1_out_4), .col1(multiplexer_1_out), .col2(multiplexer_2_out),
    .col3(multiplexer_3_out), .col4(multiplexer_4_out), .col5(multiplexer_5_out), .col6(multiplexer_7_out),
    .col7(multiplexer_6_out), .col8(multiplexer_8_out), .col9(multiplexer_10_out), .col10(multiplexer_9_out),
    .col11(multiplexer_12_out), .col12(multiplexer_11_out), .col13(multiplexer_13_out),
    .col14(multiplexer_15_out), .col15(multiplexer_14_out), .col16(multiplexer_16_out),
    .col17(multiplexer_18_out), .col18(multiplexer_17_out), .col19(multiplexer_20_out),
    .col20(multiplexer_19_out), .col21(multiplexer_21_out), .col22(multiplexer_23_out),
    .col23(multiplexer_22_out), .col24(multiplexer_24_out), .col25(multiplexer_26_out),
    .col26(multiplexer_27_out), .col27(multiplexer_29_out), .col28(multiplexer_28_out),
    .col29(multiplexer_30_out), .col30(multiplexer_31_out), .col31(paddle_shift_2_out_4));
  Paddle_Shift paddle_shift_1 (.Up(UP_out), .Reset(RESET_out), .Down(DOWN_out), .out_4(paddle_shift_1_out_4));
  Multiplexer #(.width(32), .enable("false")) multiplexer_9 (
    .in0({32{1'b0}}), .in1(X_Axis), .out(multiplexer_9_out), .sel(Y_Axis[9]));
  Multiplexer #(.width(32), .enable("false")) multiplexer_10 (
    .in0({32{1'b0}}), .in1(X_Axis), .out(multiplexer_10_out), .sel(Y_Axis[8]));
  Multiplexer #(.width(32), .enable("false")) multiplexer_11 (
    .in0({32{1'b0}}), .in1(X_Axis), .out(multiplexer_11_out), .sel(Y_Axis[11]));
  Multiplexer #(.width(32), .enable("false")) multiplexer_12 (
    .in0({32{1'b0}}), .in1(X_Axis), .out(multiplexer_12_out), .sel(Y_Axis[10]));
  Multiplexer #(.width(32), .enable("false")) multiplexer_13 (
    .in0({32{1'b0}}), .in1(X_Axis), .out(multiplexer_13_out), .sel(Y_Axis[12]));
  Multiplexer #(.width(32), .enable("false")) multiplexer_14 (
    .in0({32{1'b0}}), .in1(X_Axis), .out(multiplexer_14_out), .sel(Y_Axis[14]));
  Multiplexer #(.width(32), .enable("false")) multiplexer_15 (
    .in0({32{1'b0}}), .in1(X_Axis), .out(multiplexer_15_out), .sel(Y_Axis[13]));
  Hex_Digit_Display hex_digit_display_2 ();  // open: value, dp
  Paddle_Shift paddle_shift_2 (.Up(UP_2_out), .Reset(RESET_2_out), .Down(DOWN_2_out), .out_4(paddle_shift_2_out_4));
  Multiplexer #(.width(32), .enable("false")) multiplexer_16 (
    .in0({32{1'b0}}), .in1(X_Axis), .out(multiplexer_16_out), .sel(Y_Axis[15]));
  Button UP_2 (.out(UP_2_out));
  Button DOWN_2 (.out(DOWN_2_out));
  Multiplexer #(.width(32), .enable("false")) multiplexer_17 (
    .in0({32{1'b0}}), .in1(X_Axis), .out(multiplexer_17_out), .sel(Y_Axis[17]));
  Multiplexer #(.width(32), .enable("false")) multiplexer_18 (
    .in0({32{1'b0}}), .in1(X_Axis), .out(multiplexer_18_out), .sel(Y_Axis[16]));
  Button RESET_2 (.out(RESET_2_out));
  Multiplexer #(.width(32), .enable("false")) multiplexer_19 (
    .in0({32{1'b0}}), .in1(X_Axis), .out(multiplexer_19_out), .sel(Y_Axis[19]));
  Multiplexer #(.width(32), .enable("false")) multiplexer_20 (
    .in0({32{1'b0}}), .in1(X_Axis), .out(multiplexer_20_out), .sel(Y_Axis[18]));
  Multiplexer #(.width(32), .enable("false")) multiplexer_21 (
    .in0({32{1'b0}}), .in1(X_Axis), .out(multiplexer_21_out), .sel(Y_Axis[20]));
  Multiplexer #(.width(32), .enable("false")) multiplexer_22 (
    .in0({32{1'b0}}), .in1(X_Axis), .out(multiplexer_22_out), .sel(Y_Axis[22]));
  Multiplexer #(.width(32), .enable("false")) multiplexer_23 (
    .in0({32{1'b0}}), .in1(X_Axis), .out(multiplexer_23_out), .sel(Y_Axis[21]));
  Multiplexer #(.width(32), .enable("false")) multiplexer_24 (
    .in0({32{1'b0}}), .in1(X_Axis), .out(multiplexer_24_out), .sel(Y_Axis[23]));
  Shifter #(.width(32)) shifter_1 (.in(register_1_q), .\dist (5'b00001), .out(shifter_1_out));
  Multiplexer #(.select(2), .width(32), .enable("false")) multiplexer_25 (
    .in0(register_1_q), .in1(shifter_1_out), .in2(shifter_2_out), .out(multiplexer_25_out), .sel(button_1_out));  // open: in3
  Shifter #(.width(32), .shift("lr")) shifter_2 (.in(register_1_q), .\dist (5'b00001), .out(shifter_2_out));
  Button button_1 (.out(button_1_out[0]));
  Button button_2 (.out(button_1_out[1]));
  Multiplexer #(.width(32), .enable("false")) multiplexer_26 (
    .in0({32{1'b0}}), .in1(X_Axis), .out(multiplexer_26_out), .sel(Y_Axis[24]));
  Multiplexer #(.width(32), .enable("false")) multiplexer_27 (
    .in0({32{1'b0}}), .in1(X_Axis), .out(multiplexer_27_out), .sel(Y_Axis[25]));
  Register #(.width(32)) register_1 (.D(multiplexer_25_out), .Q(register_1_q), .clk(Clock));  // open: en, clr
  Multiplexer #(.width(32), .enable("false")) multiplexer_28 (
    .in0({32{1'b0}}), .in1(X_Axis), .out(multiplexer_28_out), .sel(Y_Axis[27]));
  Multiplexer #(.width(32), .enable("false")) multiplexer_29 (
    .in0({32{1'b0}}), .in1(X_Axis), .out(multiplexer_29_out), .sel(Y_Axis[26]));
  Multiplexer #(.width(32), .enable("false")) multiplexer_30 (
    .in0({32{1'b0}}), .in1(X_Axis), .out(multiplexer_30_out), .sel(Y_Axis[28]));
  Multiplexer #(.width(32), .enable("false")) multiplexer_31 (
    .in0({32{1'b0}}), .in1(X_Axis), .out(multiplexer_31_out), .sel(Y_Axis[29]));
endmodule

module Paddle_Shift (
  input  Up,
  input  Reset,
  input  Down,
  output [31:0] out_4
);

  wire clock_1_out, not_1_out;
  wire [31:0] controlled_buffer_1_out, multiplexer_1_out, shifter_1_out, shifter_2_out;

  Shifter #(.width(32)) shifter_1 (.in(out_4), .\dist (5'b00001), .out(shifter_1_out));
  Shifter #(.width(32), .shift("lr")) shifter_2 (.in(out_4), .\dist (5'b00001), .out(shifter_2_out));
  assign controlled_buffer_1_out = not_1_out ? multiplexer_1_out : 32'bz;  // Controlled_Buffer controlled_buffer_1
  Multiplexer #(.select(2), .width(32), .enable("false")) multiplexer_1 (
    .in0(out_4), .in1(shifter_1_out), .in2(shifter_2_out), .out(multiplexer_1_out), .sel({Down, Up}));  // open: in3
  not not_1 (not_1_out, Reset);
  Register #(.width(32)) register_1 (.D(controlled_buffer_1_out), .Q(out_4), .clk(clock_1_out));  // open: en, clr
  Clock clock_1 (.out(clock_1_out));
  assign controlled_buffer_1_out = Reset ? 32'h3c000 : 32'bz;  // Controlled_Buffer controlled_buffer_2
endmodule
