// Logisim project pongtest.circ as structural Verilog: 1 circuit, main circuit main
module main (
  input  in_1,
  input  in_2,
  input  in_3,
  input  [31:0] in_4
);

  wire clock_1_out, multiplexer_1_out;
  wire [1:0] button_2_out;
  wire [4:0] joystick_1_x, joystick_1_y;
  wire [31:0] multiplexer_2_out, register_1_q, shifter_1_out, shifter_2_out;

  // Probe on multiplexer_1_out
  Multiplexer multiplexer_1 (.in0(in_1), .in1(in_2), .out(multiplexer_1_out), .sel(in_3));  // open: en
  DotMatrix #(.matrixcols(32), .matrixrows(32)) dotmatrix_1 (
    .col0(in_4), .col1({32{1'b0}}), .col31(register_1_q));  // open: col2, col3, col4, col5, col6, col7, col8, col9, col10, col11, col12, col13, col14, col15, col16, col17, col18, col19, col20, col21, col22, col23, col24, col25, col26, col27, col28, col29, col30
  Joystick #(.bits(5)) joystick_1 (.x(joystick_1_x), .y(joystick_1_y));
  // Probe on joystick_1_x
  // Probe on joystick_1_y
  Shifter #(.width(32), .shift("lr")) shifter_1 (.in(register_1_q), .\dist (5'b00001), .out(shifter_1_out));
  Shifter #(.width(32)) shifter_2 (.in(register_1_q), .\dist (5'b00001), .out(shifter_2_out));
  Register #(.width(32)) register_1 (.D(multiplexer_2_out), .Q(register_1_q), .clk(clock_1_out));  // open: en, clr
  Clock clock_1 (.out(clock_1_out));
  Button button_1 (.out(button_2_out[1]));
  Button button_2 (.out(button_2_out[0]));
  Multiplexer #(.select(2), .width(32)) multiplexer_2 (
    .in1(shifter_1_out), .in2(shifter_2_out), .out(multiplexer_2_out), .sel(button_2_out));  // open: in0, in3, en
endmodule
